# Fritzing sketch Spear (saved by Fritzing 0.9.3b)
breadboards: 1

parts:
  R1 = Photocell (LDR) [package=THT]
  S4 = Pushbutton [package="[THT]"]
  LCD1 = LCD screen
  Componente2 = Adafruit Motor/Stepper/Servo Shield [part_number="Adafruit #1438"]
  KEYPAD1 = Membrane Matrix Keypad
  Componente5 = Adafruit TSL2591 [part_number="Adafruit #1980"]
  Componente6 = Adafruit DS1307 RTC Breakout [part_number="Adafruit #264"]
  M1 = Stepper Motor - Bipolar
  JACK1 = 2.1mm Barrel Jack with Terminal Block
  R5 = Resistor [tolerance=±5% resistance=220 package=THT]
  S5 = Pushbutton [package="[THT]"]
  R6 = Resistor [tolerance=±5% resistance=220 package=THT]
  S6 = Pushbutton [package="[THT]"]
  R7 = Resistor [tolerance=±5% resistance=220 package=THT]
  S7 = Pushbutton [package="[THT]"]
  R8 = Resistor [tolerance=±5% resistance=220 package=THT]
  S8 = Pushbutton [package="[THT]"]
  R9 = Resistor [tolerance=±5% resistance=220 package=THT]
  J1 = Piezo Speaker
  U1 = Arduino Mega 2560 (Rev3)
  R11 = Rotary Potentiometer (Small) [maximum_resistance=100kΩ package=THT]

nets:
  VDD: R1.pin_1, S4.Pin_3, S4.Pin_4, LCD1.VDD, LCD1.LED+, Componente2.+5V, Componente5.VIN, Componente6.VCC, S5.Pin_3, S5.Pin_4, S6.Pin_3, S6.Pin_4, S7.Pin_3, S7.Pin_4, S8.Pin_3, S8.Pin_4, R11.leg2
  N1: S4.Pin_1, S4.Pin_2, R5.Pin_0, U1.D7_PWM
  GND: LCD1.VSS, LCD1.R/W, LCD1.LED-, Componente2.GND, Componente5.GND, Componente6.GND, JACK1.NEG, R5.Pin_1, R6.Pin_1, R7.Pin_1, R8.Pin_1, R9.Pin_1, J1.pin1, R11.leg1
  N2: LCD1.V0, R11.wiper
  N3: LCD1.RS, U1.D8_PWM
  N4: LCD1.E, U1.D9_PWM
  N5: LCD1.DB4, U1.D10_PWM
  N6: LCD1.DB5, U1.D11_PWM
  N7: LCD1.DB6, U1.D12_PWM
  N8: LCD1.DB7, U1.D13_PWM
  N9: Componente2.M3A, M1.D
  N10: Componente2.M3B, M1.B
  N11: Componente2.M4B, M1.C
  N12: Componente2.M4A, M1.A
  N13: Componente2.AD5/SCL, Componente5.SCL, Componente6.SCL, U1.D21/SCL
  N14: Componente2.AD4/SDA, Componente5.SDA, Componente6.SDA, U1.D20/SDA
  N15: Componente2.VMOTOR, JACK1.POS
  N16: KEYPAD1.1, U1.D38
  N17: KEYPAD1.2, U1.D37
  N18: KEYPAD1.3, U1.D36
  N19: KEYPAD1.4, U1.D35
  N20: KEYPAD1.5, U1.D34
  N21: KEYPAD1.6, U1.D33
  N22: KEYPAD1.7, U1.D32
  N23: S5.Pin_1, S5.Pin_2, R6.Pin_0, U1.D6_PWM
  N24: S6.Pin_1, S6.Pin_2, R7.Pin_0, U1.D5_PWM
  N25: S7.Pin_1, S7.Pin_2, R8.Pin_0, U1.D4_PWM
  N26: S8.Pin_1, S8.Pin_2, R9.Pin_0, U1.D3_PWM
  N27: J1.pin2, U1.D46

custom parts:
  Adafruit Motor/Stepper/Servo Shield: The original Adafruit Motorshield kit is one of our most beloved kits, which is why we decided to make something even better. We have upgraded the shield kit to make the bestest, easiest way to drive DC and Stepper motors. This shield will make quick work of your next robotics project! We kept the ability to drive up to 4 DC motors or 2 stepper motors, but added many improvements: Instead of a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
  Membrane Matrix Keypad: Membrane Matrix 3x4 Keypad
  Adafruit TSL2591: When the future is dazzlingly-bright, this ultra-high-range luminosity sensor will help you measure it. The TSL2591 luminosity sensor is an advanced digital light sensor, ideal for use in a wide range of light situations. Compared to low cost CdS cells, this sensor is more precise, allowing for exact lux calculations and can be configured for different gain/timing ranges to detect light ranges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
  Adafruit DS1307 RTC Breakout: This is a great battery-backed real time clock (RTC) that allows your microcontroller project to keep track of time even if it is reprogrammed, or if the power is lost. Perfect for datalogging, clock-building, time stamping, timers and alarms, etc. The DS1307 is the most popular RTC - but it requires 5V power to work (although we've used it with 5V power and 3.3V logic successfully) PCB &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
